# Fritzing sketch pcb (saved by Fritzing 0.9.3b)
circuit board: 4.02155cm x 6.86356cm
breadboards: 1

parts:
  R1 = Resistor [tolerance=±5% resistance=10k package=THT]
  R2 = Resistor [tolerance=±5% resistance=10k package=THT]
  R3 = Resistor [tolerance=±5% resistance=10k package=THT]
  R4 = Resistor [tolerance=±5% resistance=10k package=THT]
  Q1 = Basic FET N-Channel [package="TO220 [THT]"]
  Q2 = Basic FET N-Channel [package="TO220 [THT]"]
  Pad1 = Pad [width=3 height=5 connect=center]
  Pad2 = Pad [width=3 height=5 connect=center]
  Pad3 = Pad [width=2 height=5 connect=center]
  Pad4 = Pad [width=2 height=5 connect=center]
  Pad6 = Pad [width=2 height=5 connect=center]
  Pad5 = Pad [width=2 height=5 connect=center]
  Pad7 = Pad [width=2 height=5 connect=center]
  Pad8 = Pad [width=2 height=5 connect=center]
  Pad9 = Pad [width=2 height=5 connect=center]
  Pad10 = Pad [width=2 height=5 connect=center]

nets:
  N1: R1.Pin_0, Pad3.pad
  N2: R1.Pin_1, R4.Pin_1, Q1.source, Q2.source
  N3: R2.Pin_0, R3.Pin_0, Pad8.pad
  N4: R2.Pin_1, Pad6.pad
  N5: R3.Pin_1, Pad5.pad
  N6: R4.Pin_0, Pad4.pad
  N7: Q1.drain, Pad2.pad
  N8: Q2.drain, Pad1.pad
  N9: Pad7.pad, Pad9.pad, Pad10.pad
